# Fritzing sketch diagram (saved by Fritzing 0.9.2b)
breadboards: 1

parts:
  U1 = 74HC595 SMD [package="SO16 [SMD]"]
  R4 = Resistor [tolerance=±5% resistance=220 package=THT]
  Raspberry_Pi1 = Raspberry Pi B rev2
  DI1 = 7-Segment LED Display [package=THT]
  S1 = Pushbutton [package="[SMD]"]
  S2 = Pushbutton [package="[SMD]"]

nets:
  N1: U1.Q1, DI1.cathodeF
  N2: U1.Q2, DI1.cathodeA
  N3: U1.Q3, DI1.cathodeB
  N4: U1.Q4, DI1.cathodeE
  N5: U1.Q5, DI1.cathodeD
  N6: U1.Q6, DI1.cathodeC
  N7: U1.Q7, DI1.cathodeDP
  GND: U1.GND, U1.OE, R4.Pin_0, Raspberry_Pi1.GND, S1.Pin_1, S1.Pin_2, S2.Pin_1, S2.Pin_2
  VCC: U1.MR, U1.VCC, Raspberry_Pi1.3V3
  N8: U1.SH_CP, Raspberry_Pi1.GPIO_7
  N9: U1.ST_CP, Raspberry_Pi1.GPIO_25
  N10: U1.DS, Raspberry_Pi1.GPIO_8
  N11: U1.Q0, DI1.cathodeG
  N12: R4.Pin_1, DI1.commAnode#7
  N13: Raspberry_Pi1.GPIO_23, S2.Pin_3, S2.Pin_4
  N14: Raspberry_Pi1.GPIO_24, S1.Pin_3, S1.Pin_4
